// Logisim project cpu.circ as structural Verilog: 1 circuit, main circuit cpu
module cpu (
  input  clk,
  input  [31:0] Instruction,
  input  [31:0] MemReadData,
  output [31:0] MemAddress,
  output [31:0] ProgramCounter,
  output [31:0] ra,
  output [31:0] sp,
  output [31:0] t0,
  output [31:0] t1,
  output [31:0] t2,
  output [31:0] s0,
  output [31:0] s1,
  output [31:0] a0,
  output [3:0] MemWriteMask,
  output [31:0] MemWriteData
);

  wire control_logic_1_p2, control_logic_1_p3, control_logic_1_p5, control_logic_1_p6, undriven_2,
       undriven_3, undriven_4, undriven_6;
  wire [1:0] undriven;
  wire [2:0] control_logic_1_p4;
  wire [3:0] undriven_5;
  wire [31:0] adder_1_out, adder_2_out, DataFromReg, DataToReg, imm_gen_1_immediate, Instruction_t,
       multiplexer_1_out, multiplexer_2_out, multiplexer_3_out, multiplexer_4_out, multiplexer_5_out,
       ProgramCounter_t, regfile_1_readdata1;

  Adder #(.width(32)) adder_1 (.a(ProgramCounter), .b(32'h4), .out(adder_1_out));  // open: cin, cout
  Register #(.width(32)) PC (.D(multiplexer_1_out), .clk(clk), .Q(ProgramCounter));  // open: en, clr
  Multiplexer #(.width(32)) multiplexer_1 (
    .in0(adder_1_out), .in1(MemAddress), .out(multiplexer_1_out), .sel(control_logic_1_p2));
  Multiplexer #(.width(32)) multiplexer_2 (
    .in0(Instruction), .in1(32'h13), .out(multiplexer_2_out), .sel(control_logic_1_p2));
  Register #(.width(32)) register_1 (.D(ProgramCounter), .clk(clk), .Q(ProgramCounter_t));  // open: en, clr
  Register #(.width(32)) register_2 (.D(multiplexer_2_out), .clk(clk), .Q(Instruction_t));  // open: en, clr
  Multiplexer #(.select(2), .width(32)) multiplexer_3 (
    .in1(MemAddress), .in2(DataToReg), .in3(adder_2_out), .out(multiplexer_3_out), .sel(undriven));  // open: in0
  Adder #(.width(32)) adder_2 (.a(ProgramCounter_t), .b(32'h4), .out(adder_2_out));  // open: cin, cout
  // control_logic control_logic_1: pin names not known; wires that end beside it: Instruction_t, control_logic_1_p2, control_logic_1_p3, control_logic_1_p4, control_logic_1_p5, control_logic_1_p6
  regfile regfile_1 (
    .ReadIndex1(Instruction_t[19:15]), .ReadIndex2(Instruction_t[24:20]), .WriteIndex(Instruction_t[11:7]),
    .WriteData(multiplexer_3_out), .RegWEn(control_logic_1_p3), .clk(clk), .ra(ra), .sp(sp), .t0(t0),
    .t1(t1), .t2(t2), .s0(s0), .s1(s1), .a0(a0), .ReadData1(regfile_1_readdata1), .ReadData2(DataFromReg));
  imm_gen imm_gen_1 (.Instruction(Instruction_t), .ImmSel(control_logic_1_p4), .Immediate(imm_gen_1_immediate));
  Multiplexer #(.width(32)) multiplexer_4 (
    .in0(DataFromReg), .in1(imm_gen_1_immediate), .out(multiplexer_4_out), .sel(undriven_3));
  Multiplexer #(.width(32)) multiplexer_5 (
    .in0(regfile_1_readdata1), .in1(ProgramCounter_t), .out(multiplexer_5_out), .sel(undriven_4));
  branch_comp branch_comp_1 (
    .BrData1(regfile_1_readdata1), .BrData2(DataFromReg), .BrUn(undriven_2), .BrEq(control_logic_1_p5),
    .BrLt(control_logic_1_p6));
  alu alu_1 (.A(multiplexer_5_out), .B(multiplexer_4_out), .ALUSel(undriven_5), .ALUResult(MemAddress));
  partial_load partial_load_1 (
    .Instruction(Instruction_t), .MemAddress(MemAddress), .DataFromMem(MemReadData), .DataToReg(DataToReg));
  partial_store partial_store_1 (
    .Instruction(Instruction_t), .MemAddress(MemAddress), .DataFromReg(DataFromReg), .MemWEn(undriven_6),
    .MemWriteMask(MemWriteMask), .DataToMem(MemWriteData));

  // Other names for the same wires on the sheet: Instruction1[31:0] = Instruction; rd[4:0] = Instruction_t[11:7];
  //   rs1[4:0] = Instruction_t[19:15]; rs2[4:0] = Instruction_t[24:20]; newpc[31:0] = MemAddress;
  //   ProgramCounter1[31:0] = ProgramCounter

  // Notes on the sheet:
  //   To IMEM
  //   IMEM (do **NOT** move this)
  //   From IMEM
  //   Inputs/Outputs for testing. Do **NOT** move these.
  //   It is OK to move the PC, RegFile, ALU, MEM, Branch Comp, Imm Gen, Partial Load, Partial Store and Control Logic to wherever is most convenient for you when constructing your CPU, and to delete this text
  //   To DMEM
  //   DMEM (do **NOT** move this)
  //   From DMEM
endmodule
