// Logisim project partial-store.circ as structural Verilog: 1 circuit, main circuit partial_store
module partial_store (
  input  [31:0] Instruction,
  input  [31:0] MemAddress,
  input  [31:0] DataFromReg,
  input  MemWEn,
  output [3:0] MemWriteMask,
  output [31:0] DataToMem
);

  wire [3:0] multiplexer_1_out, multiplexer_2_out, shifter_1_out;
  wire [4:0] bit_extender_1_out, bit_extender_2_out, multiplier_1_out, multiplier_2_out;
  wire [31:0] bit_extender_3_out, bit_extender_4_out, shifter_2_out, shifter_3_out;

  assign bit_extender_1_out = {{3{MemAddress[1]}}, MemAddress[1:0]};  // Bit_Extender bit_extender_1
  Multiplexer #(.select(2), .width(4)) multiplexer_1 (
    .in0(4'b0011), .in2(4'b1100), .out(multiplexer_1_out), .sel(MemAddress[1:0]));  // open: in1, in3
  Multiplier #(.width(5)) multiplier_1 (
    .a(5'b01000), .b(bit_extender_2_out), .out(multiplier_1_out));  // open: cin, cout
  Multiplier #(.width(5)) multiplier_2 (
    .a(5'b01000), .b(bit_extender_1_out), .out(multiplier_2_out));  // open: cin, cout
  Shifter #(.width(4)) shifter_1 (.in(4'b0001), .\dist (MemAddress[1:0]), .out(shifter_1_out));
  Multiplexer #(.select(3), .width(4)) multiplexer_2 (
    .in0(shifter_1_out), .in1(multiplexer_1_out), .in2(4'b1111), .out(multiplexer_2_out),
    .sel(Instruction[14:12]));  // open: in3, in4, in5, in6, in7
  assign bit_extender_2_out = {{3{MemAddress[1]}}, MemAddress[1:0]};  // Bit_Extender bit_extender_2
  Shifter #(.width(32)) shifter_2 (.in(bit_extender_4_out), .\dist (multiplier_1_out), .out(shifter_2_out));
  Multiplexer #(.width(4)) multiplexer_3 (.in0(4'b0000), .in1(multiplexer_2_out), .out(MemWriteMask), .sel(MemWEn));
  assign bit_extender_3_out = {{16{DataFromReg[15]}}, DataFromReg[15:0]};  // Bit_Extender bit_extender_3
  assign bit_extender_4_out = {{24{DataFromReg[7]}}, DataFromReg[7:0]};  // Bit_Extender bit_extender_4
  Shifter #(.width(32)) shifter_3 (.in(bit_extender_3_out), .\dist (multiplier_2_out), .out(shifter_3_out));
  Multiplexer #(.select(3), .width(32)) multiplexer_4 (
    .in0(shifter_2_out), .in1(shifter_3_out), .in2(DataFromReg), .out(DataToMem), .sel(Instruction[14:12]));  // open: in3, in4, in5, in6, in7

  // Other names for the same wires on the sheet: datab[7:0] = DataFromReg[7:0]; datah[15:0] = DataFromReg[15:0];
  //   opcode[6:0] = Instruction[6:0]; funct3[2:0] = Instruction[14:12]; funct7[6:0] = Instruction[31:25];
  //   last2[1:0] = MemAddress[1:0]

  // Notes on the sheet:
  //   INPUTS to your circuit
  //   DON'T CHANGE THE LOCATIONS OF THE INPUTS AND OUTPUTS!
  //   OUTPUT from your circuit
endmodule
