// Logisim project regfile.circ as structural Verilog: 1 circuit, main circuit regfile
module regfile (
  input  [4:0] ReadIndex1,
  input  [4:0] ReadIndex2,
  input  [4:0] WriteIndex,
  input  [31:0] WriteData,
  input  RegWEn,
  input  clk,
  output [31:0] ra,
  output [31:0] sp,
  output [31:0] t0,
  output [31:0] t1,
  output [31:0] t2,
  output [31:0] s0,
  output [31:0] s1,
  output [31:0] a0,
  output [31:0] ReadData1,
  output [31:0] ReadData2
);

  wire in1, in2, in3, in4, in5, in6, in7, in8, in9, in10, in11, in12, in13, in14, in15, in16, in17, in18,
       in19, in20, in21, in22, in23, in24, in25, in26, in27, in28, in29, in30, in31;
  wire [31:0] out3, out4, out11, out12, out13, out14, out15, out16, out17, out18, out19, out20, out21, out22,
       out23, out24, out25, out26, out27, out28, out29, out30, out31;

  Demultiplexer #(.select(5)) demultiplexer_1 (
    .out1(in1), .out2(in2), .out3(in3), .out4(in4), .out5(in5), .out6(in6), .out7(in7), .out8(in8),
    .out9(in9), .out10(in10), .out11(in11), .out12(in12), .out13(in13), .out14(in14), .out15(in15),
    .out16(in16), .out17(in17), .out18(in18), .out19(in19), .out20(in20), .out21(in21), .out22(in22),
    .out23(in23), .out24(in24), .out25(in25), .out26(in26), .out27(in27), .out28(in28), .out29(in29),
    .out30(in30), .out31(in31), .in(RegWEn), .sel(WriteIndex));  // open: out0
  Register #(.width(32)) register_1 (.D(WriteData), .en(in3), .clk(clk), .Q(out3));  // open: clr
  Register #(.width(32)) register_2 (.D(WriteData), .en(in4), .clk(clk), .Q(out4));  // open: clr
  Register #(.width(32)) register_3 (.D(WriteData), .en(in11), .clk(clk), .Q(out11));  // open: clr
  Register #(.width(32)) register_4 (.D(WriteData), .en(in12), .clk(clk), .Q(out12));  // open: clr
  Register #(.width(32)) register_5 (.D(WriteData), .en(in13), .clk(clk), .Q(out13));  // open: clr
  Register #(.width(32)) register_6 (.D(WriteData), .en(in14), .clk(clk), .Q(out14));  // open: clr
  Register #(.width(32)) register_7 (.D(WriteData), .en(in15), .clk(clk), .Q(out15));  // open: clr
  Register #(.width(32)) register_8 (.D(WriteData), .en(in16), .clk(clk), .Q(out16));  // open: clr
  Register #(.width(32)) register_9 (.D(WriteData), .en(in17), .clk(clk), .Q(out17));  // open: clr
  Register #(.width(32)) register_10 (.D(WriteData), .en(in18), .clk(clk), .Q(out18));  // open: clr
  Register #(.width(32)) register_11 (.D(WriteData), .en(in19), .clk(clk), .Q(out19));  // open: clr
  Register #(.width(32)) register_12 (.D(WriteData), .en(in20), .clk(clk), .Q(out20));  // open: clr
  Register #(.width(32)) register_13 (.D(WriteData), .en(in21), .clk(clk), .Q(out21));  // open: clr
  Register #(.width(32)) register_14 (.D(WriteData), .en(in22), .clk(clk), .Q(out22));  // open: clr
  Register #(.width(32)) register_15 (.D(WriteData), .en(in23), .clk(clk), .Q(out23));  // open: clr
  Register #(.width(32)) register_16 (.D(WriteData), .en(in24), .clk(clk), .Q(out24));  // open: clr
  Register #(.width(32)) register_17 (.D(WriteData), .en(in25), .clk(clk), .Q(out25));  // open: clr
  Register #(.width(32)) register_18 (.D(WriteData), .en(in26), .clk(clk), .Q(out26));  // open: clr
  Register #(.width(32)) register_19 (.D(WriteData), .en(in27), .clk(clk), .Q(out27));  // open: clr
  Register #(.width(32)) register_20 (.D(WriteData), .en(in28), .clk(clk), .Q(out28));  // open: clr
  Register #(.width(32)) register_21 (.D(WriteData), .en(in29), .clk(clk), .Q(out29));  // open: clr
  Register #(.width(32)) register_22 (.D(WriteData), .en(in30), .clk(clk), .Q(out30));  // open: clr
  Register #(.width(32)) register_23 (.D(WriteData), .en(in31), .clk(clk), .Q(out31));  // open: clr
  Register #(.width(32)) register_24 (.D(WriteData), .en(in1), .clk(clk), .Q(ra));  // open: clr
  Register #(.width(32)) register_25 (.D(WriteData), .en(in5), .clk(clk), .Q(t0));  // open: clr
  Register #(.width(32)) register_26 (.D(WriteData), .en(in6), .clk(clk), .Q(t1));  // open: clr
  Register #(.width(32)) register_27 (.D(WriteData), .en(in7), .clk(clk), .Q(t2));  // open: clr
  Register #(.width(32)) register_28 (.D(WriteData), .en(in8), .clk(clk), .Q(s0));  // open: clr
  Register #(.width(32)) register_29 (.D(WriteData), .en(in9), .clk(clk), .Q(s1));  // open: clr
  Register #(.width(32)) register_30 (.D(WriteData), .en(in10), .clk(clk), .Q(a0));  // open: clr
  Register #(.width(32)) register_31 (.D(WriteData), .en(in2), .clk(clk), .Q(sp));  // open: clr
  Multiplexer #(.select(5), .width(32)) multiplexer_1 (
    .in0({32{1'b0}}), .in1(ra), .in2(sp), .in3(out3), .in4(out4), .in5(t0), .in6(t1), .in7(t2), .in8(s0),
    .in9(s1), .in10(a0), .in11(out11), .in12(out12), .in13(out13), .in14(out14), .in15(out15), .in16(out16),
    .in17(out17), .in18(out18), .in19(out19), .in20(out20), .in21(out21), .in22(out22), .in23(out23),
    .in24(out24), .in25(out25), .in26(out26), .in27(out27), .in28(out28), .in29(out29), .in30(out30),
    .in31(out31), .out(ReadData1), .sel(ReadIndex1));
  Multiplexer #(.select(5), .width(32)) multiplexer_2 (
    .in0({32{1'b0}}), .in1(ra), .in2(sp), .in3(out3), .in4(out4), .in5(t0), .in6(t1), .in7(t2), .in8(s0),
    .in9(s1), .in10(a0), .in11(out11), .in12(out12), .in13(out13), .in14(out14), .in15(out15), .in16(out16),
    .in17(out17), .in18(out18), .in19(out19), .in20(out20), .in21(out21), .in22(out22), .in23(out23),
    .in24(out24), .in25(out25), .in26(out26), .in27(out27), .in28(out28), .in29(out29), .in30(out30),
    .in31(out31), .out(ReadData2), .sel(ReadIndex2));

  // Notes on the sheet:
  //   INPUTS to your circuit
  //   DON'T CHANGE THE LOCATIONS OF THE INPUTS AND OUTPUTS!
  //   These are DEBUG/TEST outputs from your circuit.
  //   OUTPUTS from your circuit
endmodule
